# Fritzing sketch Nodo1 (saved by Fritzing 0.9.3b)
breadboards: 1

parts:
  M1 = Pzem-004t
  M2 = Pzem-004t
  esp1 = ESP32 DevKitc V4
  HLK-PM2 = HLK-PM01
  U1 = 2-Channel 5v Relay Shield [package=relay-2ch5v10a]
  Power_plug1 = Power plug
  A2 = Current transformer PZCT02
  A3 = Current transformer PZCT02
  Power_plug2 = Power plug  # not connected
  J1 = Camdenboss CTB0158-2 [part_number=CTB0158-2 package=THT]
  J2 = Camdenboss CTB0158-2 [part_number=CTB0158-2 package=THT]
  S2 = Round Pushbutton
  LED1 = LED - 3mm [color="Red (633nm)" package="3 mm [THT]"]
  R1 = Resistor [tolerance=±5% resistance=330 package=THT]

nets:
  5V: M1.5V, M2.5V, esp1.5V, HLK-PM2.+Vo, R1.Pin_1
  N1: M1.RX, esp1.IO27
  N2: M1.TX, esp1.IO26
  GND: M1.GND, M2.GND, esp1.GND, HLK-PM2.-Vo, U1.GND, LED1.cathode
  N3: M1.LOUT, J2.terminal_1
  N4: M1.LIN, J2.terminal_2
  N5: M1.NIN, A3.Pin_1
  N6: M1.NOUT, A3.Pin_2
  N7: M2.RX, esp1.IO33
  N8: M2.TX, esp1.IO32
  N9: M2.LOUT, J1.terminal_1
  N10: M2.LIN, J1.terminal_2
  N11: M2.NIN, A2.Pin_1
  N12: M2.NOUT, A2.Pin_2
  N13: esp1.IO25, U1.IN2
  N14: esp1.IO14, U1.IN1
  N15: HLK-PM2.AC#0, S2.leg1
  N16: HLK-PM2.AC#1, Power_plug1.GND
  N17: U1.K1-In, Power_plug1.VCC
  N18: LED1.anode, R1.Pin_0

custom parts:
  Pzem-004t: Pzem-004t used for measuring AC voltage, current, active power, frequency, power factor and active energy, the module is without display function, the data is read through the TTL interface.
  ESP32 DevKitc V4: ESP32-DevKitC board with ESP32-WROOM-32 module. ESP32-DevKitC V4 is a small-sized ESP32-based development board produced by Espressif. Most of the pins on the ESP module are broken out to the pin headers on the board. The pins D0, D1, D2, D3, CMD and CLK are used internally for communication between ESP32 and SPI flash memory. They are grouped on both sides near the USB connector. Avoid using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
  2-Channel 5v Relay Shield: 2 Channel 5v Relay Shield w. 2x SPD-06VDC-SD-C
  Current transformer PZCT02: Current transformer PZCT02.
