# Fritzing sketch Nodo2 (saved by Fritzing 0.9.3b)
breadboards: 1

parts:
  M1 = Pzem-004t
  M2 = Pzem-004t
  HLK-PM1 = HLK-PM01
  A1 = Current transformer PZCT02
  A2 = Current transformer PZCT02
  esp1 = ESP32 DevKitc V4
  RY1 = SSR-40VA
  RY2 = SSR-40VA
  RY3 = SSR-40VA
  RY4 = SSR-40VA

nets:
  5V: M1.5V, M2.5V, HLK-PM1.+Vo
  N1: M1.RX, esp1.IO33
  N2: M1.TX, esp1.IO32
  GND: M1.GND, M2.GND, HLK-PM1.-Vo, esp1.GND, RY4.Pin_4
  N3: M1.NIN, A2.Pin_1
  N4: M1.NOUT, A2.Pin_2
  N5: M2.RX, esp1.IO27
  N6: M2.TX, esp1.IO26
  N7: M2.NIN, A1.Pin_1
  N8: M2.NOUT, A1.Pin_2
  N9: esp1.IO17, RY1.Pin_3
  N10: esp1.IO5, RY2.Pin_3
  N11: esp1.IO18, RY3.Pin_3
  N12: esp1.IO19, RY4.Pin_3

custom parts:
  Pzem-004t: Pzem-004t used for measuring AC voltage, current, active power, frequency, power factor and active energy, the module is without display function, the data is read through the TTL interface.
  Current transformer PZCT02: Current transformer PZCT02.
  ESP32 DevKitc V4: ESP32-DevKitC board with ESP32-WROOM-32 module. ESP32-DevKitC V4 is a small-sized ESP32-based development board produced by Espressif. Most of the pins on the ESP module are broken out to the pin headers on the board. The pins D0, D1, D2, D3, CMD and CLK are used internally for communication between ESP32 and SPI flash memory. They are grouped on both sides near the USB connector. Avoid using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
  SSR-40VA: SSR-40VA solid state relay.
